# Fritzing sketch sketch (saved by Fritzing 0.9.3b)
circuit board: 8.46667cm x 5.64444cm
breadboards: 1

parts:
  Raspberry_Pi_Zero1 = Raspberry Pi Zero
  S1 = Pushbutton [package="[THT]"]
  S2 = Pushbutton [package="[THT]"]
  S3 = Pushbutton [package="[THT]"]
  hc-sr1 = hc-sr04
  R1 = Resistor [tolerance=±5% resistance=1k package=THT]
  R2 = Resistor [tolerance=±5% resistance=2.2k package=THT]
  J1 = Piezo Speaker

nets:
  N1: Raspberry_Pi_Zero1.GPIO3, S3.Pin_1, S3.Pin_2
  N2: Raspberry_Pi_Zero1.GIPO4, hc-sr1.Trig
  N3: Raspberry_Pi_Zero1.GIPO17, R1.Pin_1, R2.Pin_1
  N4: Raspberry_Pi_Zero1.GIPO27, S2.Pin_1, S2.Pin_2
  N5: Raspberry_Pi_Zero1.GIPO22, J1.pin2
  N6: Raspberry_Pi_Zero1.GIPO10, S1.Pin_1, S1.Pin_2
  GND: Raspberry_Pi_Zero1.GND, S1.Pin_3, S1.Pin_4, S2.Pin_3, S2.Pin_4, S3.Pin_3, S3.Pin_4, hc-sr1.GND, R2.Pin_0, J1.pin1
  5V: Raspberry_Pi_Zero1.5V, hc-sr1.VCC
  N7: hc-sr1.Echo, R1.Pin_0
